// Logisim project S1-T1-Hardware-Implementation-Circuit.circ as structural Verilog: 1 circuit, main circuit main
module main (
  input  in_1,
  input  in_2,
  input  in_3,
  input  in_4,
  input  in_5,
  input  in_6,
  output out_7,
  output out_8,
  output out_9,
  output out_10,
  output LSB,
  output MSB
);

  wire and_1_out, and_2_out, clock_1_out, comparator_1_eq, comparator_2_eq, comparator_2_lt, comparator_3_eq,
       comparator_4_eq, comparator_5_eq, multiplexer_1_out, multiplexer_2_out, multiplexer_4_out, not_1_out,
       not_2_out, not_3_out, not_4_out, or_1_out, xor_1_out, xor_2_out, xor_3_out;
  wire [2:0] xor_4_out;

  Clock clock_1 (.out(clock_1_out));
  not not_1 (not_1_out, in_3);
  J_K_Flip_Flop #(.trigger("falling")) j_k_ff_1 (
    .J(in_6), .clk(clock_1_out), .K(in_6), .Q(LSB));  // open: Qn, preset, en, reset
  Multiplexer multiplexer_1 (.in0(in_3), .in1(not_1_out), .out(multiplexer_1_out), .sel(in_5));  // open: en
  xor xor_1 (xor_1_out, in_1, in_2, in_4);
  xor xor_2 (xor_2_out, in_3, in_1, in_4);
  xor xor_3 (xor_3_out, in_2, in_4, in_3);
  J_K_Flip_Flop #(.trigger("falling")) j_k_ff_2 (
    .J(in_6), .clk(LSB), .K(in_6), .Q(MSB));  // open: Qn, preset, en, reset
  Comparator #(.width(1)) comparator_1 (.a(1'b1), .b(MSB), .eq(comparator_1_eq));  // open: gt, lt
  Comparator #(.width(1)) comparator_2 (.a(1'b1), .b(LSB), .eq(comparator_2_eq), .lt(comparator_2_lt));  // open: gt
  xor xor_4 (xor_4_out[0], xor_1_out, in_1, in_4, in_2);
  xor xor_5 (xor_4_out[1], xor_2_out, in_1, in_4, multiplexer_1_out);
  xor xor_6 (xor_4_out[2], xor_3_out, in_2, in_4, multiplexer_1_out);
  Comparator #(.width(1)) comparator_3 (.a(1'b0), .b(xor_4_out[0]), .eq(comparator_3_eq));  // open: gt, lt
  Comparator #(.width(1)) comparator_4 (.a(1'b0), .b(xor_4_out[1]), .eq(comparator_4_eq));  // open: gt, lt
  Comparator #(.width(1)) comparator_5 (.a(1'b0), .b(xor_4_out[2]), .eq(comparator_5_eq));  // open: gt, lt
  or or_1 (or_1_out, comparator_2_eq, comparator_2_lt);
  and and_1 (and_1_out, comparator_3_eq, comparator_4_eq, comparator_5_eq);
  Multiplexer #(.select(3)) multiplexer_2 (
    .in0(1'b0), .in1(xor_4_out[0]), .in2(xor_4_out[1]), .in3(in_1), .in4(xor_4_out[2]), .in5(in_2),
    .in6(multiplexer_1_out), .in7(in_4), .out(multiplexer_2_out), .sel(xor_4_out), .en(and_2_out));
  and and_2 (and_2_out, or_1_out, not_2_out);
  not not_2 (not_2_out, comparator_1_eq);
  not not_3 (not_3_out, and_1_out);
  not not_4 (not_4_out, multiplexer_2_out);
  Multiplexer multiplexer_3 (
    .in0(multiplexer_4_out), .in1(multiplexer_1_out), .out(out_9), .sel(and_1_out), .en(and_2_out));
  Multiplexer multiplexer_4 (
    .in0(multiplexer_2_out), .in1(not_4_out), .out(multiplexer_4_out), .sel(not_3_out), .en(and_2_out));
  LED led_1 (.in(and_1_out));
  LED led_2 (.in(comparator_1_eq));

  assign out_7 = in_1;
  assign out_8 = in_2;
  assign out_10 = in_4;

  // Notes on the sheet:
  //   (d1)
  //   (d2)
  //   (d3)
  //   (d4)
  //   Data Attenuation
  //   0 if no bit is changed and 1 if changed
  //   INPUTS
  //   INPUT 1
  //   INPUT 2
  //   INPUT 3
  //   INPUT 4
  //   4. Change the counter in order to generate the number of bits lost
  //   p1
  //   p2
  //   p3
  //   d3'
  //   Counter in order to simulate the number of bits changed
  //   If the number of bits changed >= 2, then we cannot correct and recover the lost data
  //   6. Finally we can recover the lost bit by inverting it again to restore the original value
  //   Value of d3 after the attenuation
  //   if changed
  //   3. Based on the changes in the bits that changed, we consturct the new p1, p2 and p3
  //   New p1
  //   New p2
  //   New p3
  //   2. We construct the intermediate results p1,p2 and p3 and invert the bit if it has changed (in above circuit, say for example d3)
  //   HARDWARE IMPLEMENTED CIRCUIT
  //   INSTRUCTIONS :
  //   5. On looking at the binary representation of new p3, new p2, and new p1, we can find about which bit is lost (shown in the 8:1 Mux above)
  //   1. Given a set of inputs d1, d2, d3 and d4. Also we know the data attenuation (if the data got changed or not) based on the last input in the above circuit
  //   NOTE : The output of not gate becomes red
  //   since the input becomes NULL in the error case
  //   RECOVERED OUTPUTS
  //   Output 1
  //   Output 2
  //   Output 3
  //   Output 4
  //   NO ERROR
  //   (On if no data changes)
  //   If the data bits cannot be recovered only
endmodule
