// Logisim project S1-T1.circ as structural Verilog: 8 circuits, main circuit main
module main (
  input  [15:0] in_1,
  input  [15:0] in_2,
  input  [15:0] in_3,
  input  [15:0] in_4,
  input  [15:0] in_5,
  input  [15:0] in_6,
  input  [15:0] in_7,
  input  [15:0] in_8,
  input  [15:0] in_9,
  input  [15:0] in_10,
  input  [15:0] in_11,
  input  [15:0] in_12,
  input  in_13,
  input  [15:0] in_14,
  input  [15:0] in_15,
  input  [15:0] in_16,
  input  [15:0] in_17,
  output [15:0] out_18,
  output [15:0] out_19,
  output [15:0] out_20,
  output [15:0] out_21,
  output LSB,
  output out_23,
  output out_24,
  output [15:0] out_25,
  output [15:0] out_26,
  output [15:0] out_27,
  output [15:0] out_28
);

  wire and_1_out, and_2_out, and_3_out, and_4_out, and_5_out, button_1_out, button_2_out, clock_1_out,
       comparator_1_eq, comparator_2_eq, comparator_3_eq, comparator_4_eq, comparator_5_eq, comparator_6_eq,
       comparator_7_eq, comparator_8_eq, lagrangeinterpolationfindvalue_1_out_11,
       lagrangeinterpolationfindvalue_2_out_11, lagrangeinterpolationfindvalue_3_out_11, nor_1_out,
       not_1_out, not_2_out, not_3_out, or_1_out;
  wire [15:0] controlled_buffer_1_out, controlled_buffer_2_out, controlled_buffer_3_out,
       controlled_buffer_4_out, controlled_buffer_5_out, controlled_buffer_6_out, controlled_buffer_7_out,
       controlled_buffer_8_out, encrypter_parity_generator_1_encrypted_y1,
       encrypter_parity_generator_1_encrypted_y2, encrypter_parity_generator_1_encrypted_y3,
       encrypter_parity_generator_1_encrypted_y4, encrypter_parity_generator_1_y5,
       encrypter_parity_generator_1_y6, encrypter_parity_generator_2_encrypted_y1,
       encrypter_parity_generator_2_encrypted_y2, encrypter_parity_generator_2_encrypted_y3,
       encrypter_parity_generator_2_encrypted_y4, encrypter_parity_generator_2_y5,
       encrypter_parity_generator_2_y6, lagrangeinterpolationfindvalue_1_out_10,
       lagrangeinterpolationfindvalue_2_out_10, lagrangeinterpolationfindvalue_3_out_10, multiplexer_1_out,
       multiplexer_2_out, multiplexer_3_out, negator_1_out, negator_2_out, negator_3_out, register_1_q,
       register_2_q, register_3_q, register_4_q;

  Clock clock_1 (.out(clock_1_out));
  J_K_Flip_Flop j_k_ff_1 (.J(in_13), .clk(clock_1_out), .K(in_13), .Q(LSB));  // open: Qn, preset, en, reset
  or or_1 (or_1_out, out_24, LSB);
  J_K_Flip_Flop j_k_ff_2 (.J(LSB), .clk(clock_1_out), .K(or_1_out), .Q(out_23));  // open: Qn, preset, en, reset
  not not_1 (not_1_out, LSB);
  not not_2 (not_2_out, out_23);
  and and_1 (and_1_out, out_23, LSB);
  J_K_Flip_Flop j_k_ff_3 (.J(and_1_out), .clk(clock_1_out), .K(out_23), .Q(out_24));  // open: Qn, preset, en, reset
  not not_3 (not_3_out, out_24);
  and and_2 (and_2_out, not_1_out, out_23, not_3_out);
  and and_3 (and_3_out, LSB, not_2_out, not_3_out);
  Button button_1 (.out(button_1_out));
  Button button_2 (.out(button_2_out));
  nor nor_1 (nor_1_out, and_2_out, and_3_out);
  Register #(.width(16)) register_1 (.D(in_1), .Q(register_1_q), .clk(button_1_out), .clr(button_2_out));  // open: en
  Register #(.width(16)) register_2 (.D(in_5), .Q(register_2_q), .clk(button_1_out), .clr(button_2_out));  // open: en
  Register #(.width(16)) register_3 (.D(in_8), .Q(register_3_q), .clk(button_1_out), .clr(button_2_out));  // open: en
  Register #(.width(16)) register_4 (.D(in_10), .Q(register_4_q), .clk(button_1_out), .clr(button_2_out));  // open: en
  Encrypter_Parity_generator encrypter_parity_generator_1 (
    .y1(in_1), .y2(in_5), .y3(in_8), .y4(in_10), .public_key(in_11),
    .Encrypted_y1(encrypter_parity_generator_1_encrypted_y1),
    .Encrypted_y2(encrypter_parity_generator_1_encrypted_y2),
    .Encrypted_y3(encrypter_parity_generator_1_encrypted_y3),
    .Encrypted_y4(encrypter_parity_generator_1_encrypted_y4), .y5(encrypter_parity_generator_1_y5),
    .y6(encrypter_parity_generator_1_y6));
  Encrypter_Parity_generator encrypter_parity_generator_2 (
    .y1(in_1), .y2(in_5), .y3(in_8), .y4(in_10), .public_key(in_11),
    .Encrypted_y1(encrypter_parity_generator_2_encrypted_y1),
    .Encrypted_y2(encrypter_parity_generator_2_encrypted_y2),
    .Encrypted_y3(encrypter_parity_generator_2_encrypted_y3),
    .Encrypted_y4(encrypter_parity_generator_2_encrypted_y4), .y5(encrypter_parity_generator_2_y5),
    .y6(encrypter_parity_generator_2_y6));
  LagrangeInterpolationFindValue lagrangeinterpolationfindvalue_1 (
    .in_1(in_2), .in_2(in_3), .in_3(in_4), .in_4(in_6), .in_5(in_7),
    .in_6(encrypter_parity_generator_1_encrypted_y1), .in_7(encrypter_parity_generator_1_encrypted_y3),
    .in_8(encrypter_parity_generator_1_y5), .in_9(encrypter_parity_generator_1_y6),
    .out_10(lagrangeinterpolationfindvalue_1_out_10), .out_11(lagrangeinterpolationfindvalue_1_out_11));
  LagrangeInterpolationFindValue lagrangeinterpolationfindvalue_2 (
    .in_1(in_9), .in_2(in_3), .in_3(in_4), .in_4(in_6), .in_5(in_7),
    .in_6(encrypter_parity_generator_1_encrypted_y1), .in_7(encrypter_parity_generator_1_encrypted_y3),
    .in_8(encrypter_parity_generator_1_y5), .in_9(encrypter_parity_generator_1_y6),
    .out_10(lagrangeinterpolationfindvalue_2_out_10), .out_11(lagrangeinterpolationfindvalue_2_out_11));
  LagrangeInterpolationFindValue lagrangeinterpolationfindvalue_3 (
    .in_1(in_12), .in_2(in_14), .in_3(in_15), .in_4(in_16), .in_5(in_17),
    .in_6(encrypter_parity_generator_2_encrypted_y1), .in_7(encrypter_parity_generator_2_encrypted_y3),
    .in_8(encrypter_parity_generator_2_y5), .in_9(encrypter_parity_generator_2_y6),
    .out_10(lagrangeinterpolationfindvalue_3_out_10), .out_11(lagrangeinterpolationfindvalue_3_out_11));
  Negator #(.width(16)) negator_1 (.in(lagrangeinterpolationfindvalue_1_out_10), .out(negator_1_out));
  Negator #(.width(16)) negator_2 (.in(lagrangeinterpolationfindvalue_2_out_10), .out(negator_2_out));
  Negator #(.width(16)) negator_3 (.in(lagrangeinterpolationfindvalue_3_out_10), .out(negator_3_out));
  Multiplexer #(.width(16)) multiplexer_1 (
    .in0(lagrangeinterpolationfindvalue_1_out_10), .in1(negator_1_out), .out(multiplexer_1_out),
    .sel(lagrangeinterpolationfindvalue_1_out_11));  // open: en
  Multiplexer #(.width(16)) multiplexer_2 (
    .in0(lagrangeinterpolationfindvalue_2_out_10), .in1(negator_2_out), .out(multiplexer_2_out),
    .sel(lagrangeinterpolationfindvalue_2_out_11));  // open: en
  Multiplexer #(.width(16)) multiplexer_3 (
    .in0(lagrangeinterpolationfindvalue_3_out_10), .in1(negator_3_out), .out(multiplexer_3_out),
    .sel(lagrangeinterpolationfindvalue_3_out_11));  // open: en
  assign controlled_buffer_1_out = and_2_out ? register_1_q : 16'bz;  // Controlled_Buffer controlled_buffer_1
  assign controlled_buffer_2_out = and_2_out ? register_2_q : 16'bz;  // Controlled_Buffer controlled_buffer_2
  Decryptor decryptor_1 (
    .in_1(encrypter_parity_generator_1_encrypted_y1), .in_2(multiplexer_1_out),
    .in_3(encrypter_parity_generator_1_encrypted_y3), .in_4(multiplexer_2_out), .in_5(in_11), .out_6(out_18),
    .out_7(out_19), .out_8(out_20), .out_9(out_21));
  assign controlled_buffer_3_out = and_2_out ? register_4_q : 16'bz;  // Controlled_Buffer controlled_buffer_3
  Decryptor decryptor_2 (
    .in_1(encrypter_parity_generator_2_encrypted_y1), .in_2(multiplexer_3_out),
    .in_3(encrypter_parity_generator_2_encrypted_y3), .in_4(encrypter_parity_generator_2_encrypted_y4),
    .in_5(in_11), .out_6(out_25), .out_7(out_26), .out_8(out_27), .out_9(out_28));
  assign controlled_buffer_4_out = and_2_out ? register_3_q : 16'bz;  // Controlled_Buffer controlled_buffer_4
  Comparator #(.width(16)) comparator_1 (
    .a(controlled_buffer_3_out), .b(out_21), .eq(comparator_1_eq));  // open: gt, lt
  Comparator #(.width(16)) comparator_2 (
    .a(controlled_buffer_1_out), .b(out_18), .eq(comparator_2_eq));  // open: gt, lt
  Comparator #(.width(16)) comparator_3 (
    .a(controlled_buffer_2_out), .b(out_19), .eq(comparator_3_eq));  // open: gt, lt
  Comparator #(.width(16)) comparator_4 (
    .a(controlled_buffer_4_out), .b(out_20), .eq(comparator_4_eq));  // open: gt, lt
  assign controlled_buffer_5_out = and_3_out ? register_1_q : 16'bz;  // Controlled_Buffer controlled_buffer_5
  assign controlled_buffer_6_out = and_3_out ? register_2_q : 16'bz;  // Controlled_Buffer controlled_buffer_6
  assign controlled_buffer_7_out = and_3_out ? register_3_q : 16'bz;  // Controlled_Buffer controlled_buffer_7
  assign controlled_buffer_8_out = and_3_out ? register_4_q : 16'bz;  // Controlled_Buffer controlled_buffer_8
  LED led_1 (.in(and_4_out));
  and and_4 (and_4_out, comparator_2_eq, comparator_3_eq, comparator_1_eq);
  Comparator #(.width(16)) comparator_5 (
    .a(controlled_buffer_5_out), .b(out_25), .eq(comparator_5_eq));  // open: gt, lt
  Comparator #(.width(16)) comparator_6 (
    .a(out_26), .b(controlled_buffer_6_out), .eq(comparator_6_eq));  // open: gt, lt
  Comparator #(.width(16)) comparator_7 (
    .a(controlled_buffer_7_out), .b(out_27), .eq(comparator_7_eq));  // open: gt, lt
  Comparator #(.width(16)) comparator_8 (
    .a(controlled_buffer_8_out), .b(out_28), .eq(comparator_8_eq));  // open: gt, lt
  LED led_2 (.in(nor_1_out));
  LED led_3 (.in(and_5_out));
  and and_5 (and_5_out, comparator_5_eq, comparator_6_eq, comparator_7_eq, comparator_8_eq);

  // Notes on the sheet:
  //   Members :
  //   Instructions
  //   Set the inputs by selecting y1 y2 y3 y4 and key of your choice and press set inputs
  //   Keep all the inputs to be 4 bits only, we have used 16 bit inputs for handling the overflow conditions
  //   Set the value from the synchronous counter in order to demonstrate the amount of bits lost
  //   After this put the values of the indices lost as indicated where say the 2nd and 4th value are lost
  //   After setting the values using the counter y1' y2' y3' y4' are the outputs
  //   Check the three LED lights to see if the data is recovered or not for every case 
  //   Akshat Bharara - 231CS110
  //   Dev Prajapati - 231CS120
  //   Vatsal Jay Gandhi - 231CS164
  //   Before starting reset the given inputs by the reset inputs button
  //   SYNCHRONOUS COUNTER FROM VALUES 1 TO 6
  //   This represents the number of bits lost during transmission of data
  //   If the number of bits lost exceed 2 then we cannot recover the sent data
  //   MSB
  //   SET INPUTS
  //   RESET INPUTS
  //   y1
  //   y2
  //   y3
  //   y4
  //   Key
  //   INPUTS
  //   1,3,5,6
  //   X
  //   X
  //   Let the 2nd and 4th value be lost
  //   Let the 2nd value be lost
  //   4 (Index value to be found)
  //   1,3,5,6
  //   X
  //   2 (Index value to be found)
  //   2 (Index value to be found)
  //   Generating values for Lagrange Interpolation
  //   S1-T1-Reed-Solomon-Codes
  //   Generating values for Lagrange Interpolation
  //   Generating values for Lagrange Interpolation
  //   y4 (recovered)
  //   y2 (recovered)
  //   y2 (recovered)
  //   Value 4 regenerated
  //   Value 1 regenerated
  //   Value 2 regenerated
  //   Value 3 regenerated
  //   OUTPUTS
  //   y1'
  //   y2'
  //   y3'
  //   y4'
  //   OUTPUTS
  //   y1'
  //   y2'
  //   y3'
  //   y4'
  //   Data cannot be recovered
endmodule

module ProdOfSubtr (
  input  [15:0] in_1,
  input  [15:0] in_2,
  input  [15:0] in_3,
  input  [15:0] in_4,
  output [15:0] out_5,
  output out_6
);

  wire subtractor_1_bout, subtractor_2_bout, subtractor_3_bout, xor_1_out;
  wire [15:0] multiplexer_1_out, multiplexer_2_out, multiplexer_3_out, multiplier_1_out, subtractor_1_out,
       subtractor_2_out, subtractor_3_out, subtractor_4_out, subtractor_5_out, subtractor_6_out;

  Subtractor #(.width(16)) subtractor_1 (
    .a(in_1), .b(in_2), .out(subtractor_1_out), .bin(1'b0), .bout(subtractor_1_bout));
  Subtractor #(.width(16)) subtractor_2 (
    .a(in_1), .b(in_3), .out(subtractor_2_out), .bin(1'b0), .bout(subtractor_2_bout));
  Subtractor #(.width(16)) subtractor_3 (
    .a(in_1), .b(in_4), .out(subtractor_3_out), .bin(1'b0), .bout(subtractor_3_bout));
  Subtractor #(.width(16)) subtractor_4 (
    .a({16{1'b0}}), .b(subtractor_1_out), .out(subtractor_4_out));  // open: bin, bout
  Multiplexer #(.width(16)) multiplexer_1 (
    .in0(subtractor_1_out), .in1(subtractor_4_out), .out(multiplexer_1_out), .sel(subtractor_1_bout));  // open: en
  Subtractor #(.width(16)) subtractor_5 (
    .a({16{1'b0}}), .b(subtractor_2_out), .out(subtractor_5_out));  // open: bin, bout
  Subtractor #(.width(16)) subtractor_6 (
    .a({16{1'b0}}), .b(subtractor_3_out), .out(subtractor_6_out));  // open: bin, bout
  Multiplexer #(.width(16)) multiplexer_2 (
    .in0(subtractor_2_out), .in1(subtractor_5_out), .out(multiplexer_2_out), .sel(subtractor_2_bout));  // open: en
  Multiplexer #(.width(16)) multiplexer_3 (
    .in0(subtractor_3_out), .in1(subtractor_6_out), .out(multiplexer_3_out), .sel(subtractor_3_bout));  // open: en
  Multiplier #(.width(16)) multiplier_1 (
    .a(multiplexer_1_out), .b(multiplexer_2_out), .out(multiplier_1_out));  // open: cin, cout
  Multiplier #(.width(16)) multiplier_2 (.a(multiplier_1_out), .b(multiplexer_3_out), .out(out_5));  // open: cin, cout
  xor xor_1 (xor_1_out, subtractor_1_bout, subtractor_2_bout);
  xor xor_2 (out_6, subtractor_3_bout, xor_1_out);

  // Notes on the sheet:
  //   x_input
  //   x2
  //   x3
  //   x4
  //   Evaluating Expression (x_input - x2)(x_input - x3)(x_input - x4)
  //   Absolute vaue for the expression
  //   (x_input - x2)(x_input - x3)(x_nput - x4)
  //   Working :
  //   Given the inputs as x_input, x2, x3 and x4, this subcircuit finds the value of the expression
  //   (x_input-x2)*(x_input-x3)*(x_input-x4)
  //   0 if positive and 1 if negative
  //   This will significantly help us in finding the value of the numerator and denominator of the lagrange polynomial.
endmodule

module ImproperFractionTerm (
  input  [15:0] in_1,
  input  [15:0] in_2,
  input  [15:0] in_3,
  input  [15:0] in_4,
  input  [15:0] in_5,
  input  [15:0] in_6,
  output [15:0] out_7,
  output [15:0] out_8,
  output out_9
);

  wire prodofsubtr_1_out_6, prodofsubtr_2_out_6, xor_1_out;
  wire [15:0] multiplexer_1_out, negator_1_out, prodofsubtr_1_out_5;

  ProdOfSubtr prodofsubtr_1 (
    .in_1(in_1), .in_2(in_3), .in_3(in_4), .in_4(in_5), .out_5(prodofsubtr_1_out_5),
    .out_6(prodofsubtr_1_out_6));
  Negator #(.width(16)) negator_1 (.in(in_6), .out(negator_1_out));
  ProdOfSubtr prodofsubtr_2 (
    .in_1(in_2), .in_2(in_3), .in_3(in_4), .in_4(in_5), .out_5(out_8), .out_6(prodofsubtr_2_out_6));
  Multiplexer #(.width(16)) multiplexer_1 (
    .in0(in_6), .in1(negator_1_out), .out(multiplexer_1_out), .sel(in_6[15]));  // open: en
  Multiplier #(.width(16)) multiplier_1 (
    .a(prodofsubtr_1_out_5), .b(multiplexer_1_out), .out(out_7));  // open: cin, cout
  xor xor_1 (xor_1_out, prodofsubtr_1_out_6, prodofsubtr_2_out_6);
  xor xor_2 (out_9, xor_1_out, in_6[15]);

  // Notes on the sheet:
  //   x_input
  //   x1
  //   x2
  //   x3
  //   x4
  //   y1
  //   Write y1 in 2s complement if negative
  //   Evaluating Each Lagrange Interpolation Basis Polynomial (Li)
  //   Absolute Value of Denominator
  //   Absolute Value of Numerator of Li
  //   1 for -ve and 0 for +ve
  //   Working :
  //   Here in this subcircuit, we are finding the value of the 
  //   numerator and denominator for each term in the lagrange basis polynomial. 
  //   We also are finding out the sign of the term.
endmodule

module LCMofDenominator_NumeratorUpdation (
  input  [15:0] in_1,
  input  [15:0] in_2,
  input  [15:0] in_3,
  input  [15:0] in_4,
  input  [15:0] in_5,
  input  [15:0] in_6,
  input  [15:0] in_7,
  input  [15:0] in_8,
  input  [15:0] in_9,
  output [31:0] out_10,
  output [31:0] out_11,
  output Num1_Sign,
  output [31:0] out_13,
  output Num2_Sign,
  output [31:0] out_15,
  output Num3_Sign,
  output [31:0] out_17,
  output Num4_Sign
);

  wire [15:0] improperfractionterm_1_out_7, improperfractionterm_1_out_8, improperfractionterm_2_out_7,
       improperfractionterm_2_out_8, improperfractionterm_3_out_7, improperfractionterm_3_out_8,
       improperfractionterm_4_out_7, improperfractionterm_4_out_8;
  wire [31:0] bit_extender_1_out, bit_extender_2_out, bit_extender_3_out, bit_extender_4_out,
       bit_extender_5_out, bit_extender_6_out, bit_extender_7_out, bit_extender_8_out, divider_1_out,
       divider_2_out, divider_3_out, divider_4_out, multiplier_1_out, multiplier_2_out;

  ImproperFractionTerm improperfractionterm_1 (
    .in_1(in_1), .in_2(in_2), .in_3(in_3), .in_4(in_4), .in_5(in_5), .in_6(in_6),
    .out_7(improperfractionterm_1_out_7), .out_8(improperfractionterm_1_out_8), .out_9(Num1_Sign));
  assign bit_extender_1_out = {{16{1'b0}}, improperfractionterm_1_out_7};  // Bit_Extender bit_extender_1
  assign bit_extender_2_out = {{16{1'b0}}, improperfractionterm_1_out_8};  // Bit_Extender bit_extender_2
  ImproperFractionTerm improperfractionterm_2 (
    .in_1(in_1), .in_2(in_3), .in_3(in_2), .in_4(in_4), .in_5(in_5), .in_6(in_7),
    .out_7(improperfractionterm_2_out_7), .out_8(improperfractionterm_2_out_8), .out_9(Num2_Sign));
  assign bit_extender_3_out = {{16{1'b0}}, improperfractionterm_2_out_7};  // Bit_Extender bit_extender_3
  ImproperFractionTerm improperfractionterm_3 (
    .in_1(in_1), .in_2(in_4), .in_3(in_2), .in_4(in_3), .in_5(in_5), .in_6(in_8),
    .out_7(improperfractionterm_3_out_7), .out_8(improperfractionterm_3_out_8), .out_9(Num3_Sign));
  assign bit_extender_4_out = {{16{1'b0}}, improperfractionterm_2_out_8};  // Bit_Extender bit_extender_4
  assign bit_extender_5_out = {{16{1'b0}}, improperfractionterm_3_out_8};  // Bit_Extender bit_extender_5
  assign bit_extender_6_out = {{16{1'b0}}, improperfractionterm_4_out_8};  // Bit_Extender bit_extender_6
  ImproperFractionTerm improperfractionterm_4 (
    .in_1(in_1), .in_2(in_5), .in_3(in_2), .in_4(in_3), .in_5(in_4), .in_6(in_9),
    .out_7(improperfractionterm_4_out_7), .out_8(improperfractionterm_4_out_8), .out_9(Num4_Sign));
  assign bit_extender_7_out = {{16{1'b0}}, improperfractionterm_3_out_7};  // Bit_Extender bit_extender_7
  assign bit_extender_8_out = {{16{1'b0}}, improperfractionterm_4_out_7};  // Bit_Extender bit_extender_8
  Multiplier #(.width(32)) multiplier_1 (
    .a(bit_extender_2_out), .b(bit_extender_5_out), .out(multiplier_1_out));  // open: cin, cout
  Multiplier #(.width(32)) multiplier_2 (
    .a(bit_extender_6_out), .b(bit_extender_4_out), .out(multiplier_2_out));  // open: cin, cout
  Divider #(.width(32)) divider_1 (.a(out_10), .b(bit_extender_2_out), .out(divider_1_out));  // open: upper, rem
  Divider #(.width(32)) divider_2 (.a(out_10), .b(bit_extender_4_out), .out(divider_2_out));  // open: upper, rem
  Divider #(.width(32)) divider_3 (.a(out_10), .b(bit_extender_5_out), .out(divider_3_out));  // open: upper, rem
  Divider #(.width(32)) divider_4 (.a(out_10), .b(bit_extender_6_out), .out(divider_4_out));  // open: upper, rem
  Multiplier #(.width(32)) multiplier_3 (.a(multiplier_1_out), .b(multiplier_2_out), .out(out_10));  // open: cin, cout
  Multiplier #(.width(32)) multiplier_4 (.a(divider_1_out), .b(bit_extender_1_out), .out(out_11));  // open: cin, cout
  Multiplier #(.width(32)) multiplier_5 (.a(divider_2_out), .b(bit_extender_3_out), .out(out_13));  // open: cin, cout
  Multiplier #(.width(32)) multiplier_6 (.a(divider_3_out), .b(bit_extender_7_out), .out(out_15));  // open: cin, cout
  Multiplier #(.width(32)) multiplier_7 (.a(divider_4_out), .b(bit_extender_8_out), .out(out_17));  // open: cin, cout

  // Notes on the sheet:
  //   x_input
  //   x1
  //   x2
  //   x3
  //   x4
  //   y1
  //   y2
  //   y3
  //   y4
  //   N1/D1
  //   N2/D2
  //   N3/D3
  //   Evaluating each term of the Lagrange Interpolation Polynomial (yi*Li)
  //   N4/D4
  //   Working :
  //   We are finding each term of the lagrange polynomial, and evaluating the common denominator of all these terms. 
  //   In this subcircuit, we also update the numerator depending on the common denominator calculated. 
  //   LCM of Denominators
  //   (NOTE : All Numerators are Absolute Values)
  //   LCM Of Denominators
  //   Numerator1 After Taking LCM
  //   Numerator2 After Taking LCM
  //   Numerator3 After Taking LCM
  //   Numerator4 After Taking LCM
endmodule

module SummationOfAllParts_FractionDivision (
  input  [15:0] in_1,
  input  [15:0] in_2,
  input  [15:0] in_3,
  input  [15:0] in_4,
  input  [15:0] in_5,
  input  [15:0] in_6,
  input  [15:0] in_7,
  input  [15:0] in_8,
  input  [15:0] in_9,
  output [15:0] out_10,
  output Sign_of_Output
);

  wire lcmofdenominator_numeratorupdation_1_num1_sign, lcmofdenominator_numeratorupdation_1_num2_sign,
       lcmofdenominator_numeratorupdation_1_num3_sign, lcmofdenominator_numeratorupdation_1_num4_sign;
  wire [30:0] adder_3_out;
  wire [31:0] adder_1_out, adder_2_out, divider_1_out, lcmofdenominator_numeratorupdation_1_out_10,
       lcmofdenominator_numeratorupdation_1_out_11, lcmofdenominator_numeratorupdation_1_out_13,
       lcmofdenominator_numeratorupdation_1_out_15, lcmofdenominator_numeratorupdation_1_out_17,
       multiplexer_1_out, multiplexer_2_out, multiplexer_3_out, multiplexer_4_out, multiplexer_5_out,
       negator_1_out, negator_2_out, negator_3_out, negator_4_out, negator_5_out;

  LCMofDenominator_NumeratorUpdation lcmofdenominator_numeratorupdation_1 (
    .in_1(in_1), .in_2(in_2), .in_3(in_3), .in_4(in_4), .in_5(in_5), .in_6(in_6), .in_7(in_7), .in_8(in_8),
    .in_9(in_9), .out_10(lcmofdenominator_numeratorupdation_1_out_10),
    .out_11(lcmofdenominator_numeratorupdation_1_out_11),
    .Num1_Sign(lcmofdenominator_numeratorupdation_1_num1_sign),
    .out_13(lcmofdenominator_numeratorupdation_1_out_13),
    .Num2_Sign(lcmofdenominator_numeratorupdation_1_num2_sign),
    .out_15(lcmofdenominator_numeratorupdation_1_out_15),
    .Num3_Sign(lcmofdenominator_numeratorupdation_1_num3_sign),
    .out_17(lcmofdenominator_numeratorupdation_1_out_17),
    .Num4_Sign(lcmofdenominator_numeratorupdation_1_num4_sign));
  Negator #(.width(32)) negator_1 (.in(lcmofdenominator_numeratorupdation_1_out_11), .out(negator_1_out));
  Multiplexer #(.width(32)) multiplexer_1 (
    .in0(lcmofdenominator_numeratorupdation_1_out_11), .in1(negator_1_out), .out(multiplexer_1_out),
    .sel(lcmofdenominator_numeratorupdation_1_num1_sign));  // open: en
  Negator #(.width(32)) negator_2 (.in(lcmofdenominator_numeratorupdation_1_out_13), .out(negator_2_out));
  Negator #(.width(32)) negator_3 (.in(lcmofdenominator_numeratorupdation_1_out_15), .out(negator_3_out));
  Negator #(.width(32)) negator_4 (.in(lcmofdenominator_numeratorupdation_1_out_17), .out(negator_4_out));
  Adder #(.width(32)) adder_1 (.a(multiplexer_1_out), .b(multiplexer_2_out), .out(adder_1_out));  // open: cin, cout
  Multiplexer #(.width(32)) multiplexer_2 (
    .in0(lcmofdenominator_numeratorupdation_1_out_13), .in1(negator_2_out), .out(multiplexer_2_out),
    .sel(lcmofdenominator_numeratorupdation_1_num2_sign));  // open: en
  Multiplexer #(.width(32)) multiplexer_3 (
    .in0(lcmofdenominator_numeratorupdation_1_out_15), .in1(negator_3_out), .out(multiplexer_3_out),
    .sel(lcmofdenominator_numeratorupdation_1_num3_sign));  // open: en
  Multiplexer #(.width(32)) multiplexer_4 (
    .in0(lcmofdenominator_numeratorupdation_1_out_17), .in1(negator_4_out), .out(multiplexer_4_out),
    .sel(lcmofdenominator_numeratorupdation_1_num4_sign));  // open: en
  Adder #(.width(32)) adder_2 (.a(multiplexer_3_out), .b(multiplexer_4_out), .out(adder_2_out));  // open: cin, cout
  Adder #(.width(32)) adder_3 (
    .a(adder_1_out), .b(adder_2_out), .out({Sign_of_Output, adder_3_out}));  // open: cin, cout
  Negator #(.width(32)) negator_5 (.in({Sign_of_Output, adder_3_out}), .out(negator_5_out));
  Divider #(.width(32)) divider_1 (
    .a(multiplexer_5_out), .b(lcmofdenominator_numeratorupdation_1_out_10), .out(divider_1_out));  // open: upper, rem
  Multiplexer #(.width(32)) multiplexer_5 (
    .in0({Sign_of_Output, adder_3_out}), .in1(negator_5_out), .out(multiplexer_5_out), .sel(Sign_of_Output));  // open: en
  Bit_Extender #(.in_width(32)) bit_extender_1 (.in(divider_1_out), .out(out_10));

  // Notes on the sheet:
  //   x_input
  //   x1
  //   x2
  //   x3
  //   x4
  //   y1
  //   y2
  //   y3
  //   y4
  //   Finding the Value of the Lagrange Polynomial at x_input
  //   Final LCM Denominator
  //   Working :
  //   This subcircuit finds the value of the polynomial at a particular value.
  //   Final Numerator
  //   Absolute Value of the Summed Numerator
  //   Sign of the summed Numerator
  //   Absolute Value of Output
endmodule

// Lagrange
module LagrangeInterpolationFindValue (
  input  [15:0] in_1,
  input  [15:0] in_2,
  input  [15:0] in_3,
  input  [15:0] in_4,
  input  [15:0] in_5,
  input  [15:0] in_6,
  input  [15:0] in_7,
  input  [15:0] in_8,
  input  [15:0] in_9,
  output [15:0] out_10,
  output out_11
);

  SummationOfAllParts_FractionDivision summationofallparts_fractiondivision_1 (
    .in_1(in_1), .in_2(in_2), .in_3(in_3), .in_4(in_4), .in_5(in_5), .in_6(in_6), .in_7(in_7), .in_8(in_8),
    .in_9(in_9), .out_10(out_10), .Sign_of_Output(out_11));

  // Notes on the sheet:
  //   x_input
  //   x1
  //   x2
  //   x3
  //   x4
  //   y1
  //   y2
  //   y3
  //   y4
  //   Final Value of the Lagrange Polynomial
  //   Y_output (Absolute Value)
  //   Sign Of the Output
  //   1 for Negative and 0 for Positive
endmodule

// Encrypter
module Encrypter_Parity_generator (
  input  [15:0] y1,
  input  [15:0] y2,
  input  [15:0] y3,
  input  [15:0] y4,
  input  [15:0] public_key,
  output [15:0] Encrypted_y1,
  output [15:0] Encrypted_y2,
  output [15:0] Encrypted_y3,
  output [15:0] Encrypted_y4,
  output [15:0] y5,
  output [15:0] y6
);

  wire lagrangeinterpolationfindvalue_1_out_11, lagrangeinterpolationfindvalue_2_out_11;
  wire [15:0] adder_1_out, adder_2_out, adder_3_out, adder_4_out, lagrangeinterpolationfindvalue_1_out_10,
       lagrangeinterpolationfindvalue_2_out_10, negator_1_out, negator_2_out;

  Adder #(.width(16)) adder_1 (.a(y1), .b(public_key), .out(adder_1_out));  // open: cin, cout
  Adder #(.width(16)) adder_2 (.a(y2), .b(public_key), .out(adder_2_out));  // open: cin, cout
  Adder #(.width(16)) adder_3 (.a(y3), .b(public_key), .out(adder_3_out));  // open: cin, cout
  Adder #(.width(16)) adder_4 (.a(y4), .b(public_key), .out(adder_4_out));  // open: cin, cout
  Divider #(.width(16)) divider_1 (.a(adder_1_out), .b(16'h10), .rem(Encrypted_y1));  // open: out, upper
  Divider #(.width(16)) divider_2 (.a(adder_2_out), .b(16'h10), .rem(Encrypted_y2));  // open: out, upper
  Divider #(.width(16)) divider_3 (.a(adder_3_out), .b(16'h10), .rem(Encrypted_y3));  // open: out, upper
  Divider #(.width(16)) divider_4 (.a(adder_4_out), .b(16'h10), .rem(Encrypted_y4));  // open: out, upper
  LagrangeInterpolationFindValue lagrangeinterpolationfindvalue_1 (
    .in_1(16'h5), .in_2(16'h1), .in_3(16'h2), .in_4(16'h3), .in_5(16'h4), .in_6(Encrypted_y1),
    .in_7(Encrypted_y2), .in_8(Encrypted_y3), .in_9(Encrypted_y4),
    .out_10(lagrangeinterpolationfindvalue_1_out_10), .out_11(lagrangeinterpolationfindvalue_1_out_11));
  LagrangeInterpolationFindValue lagrangeinterpolationfindvalue_2 (
    .in_1(16'h6), .in_2(16'h1), .in_3(16'h2), .in_4(16'h3), .in_5(16'h4), .in_6(Encrypted_y1),
    .in_7(Encrypted_y2), .in_8(Encrypted_y3), .in_9(Encrypted_y4),
    .out_10(lagrangeinterpolationfindvalue_2_out_10), .out_11(lagrangeinterpolationfindvalue_2_out_11));
  Negator #(.width(16)) negator_1 (.in(lagrangeinterpolationfindvalue_1_out_10), .out(negator_1_out));
  Negator #(.width(16)) negator_2 (.in(lagrangeinterpolationfindvalue_2_out_10), .out(negator_2_out));
  Multiplexer #(.width(16)) multiplexer_1 (
    .in0(lagrangeinterpolationfindvalue_1_out_10), .in1(negator_1_out), .out(y5),
    .sel(lagrangeinterpolationfindvalue_1_out_11));  // open: en
  Multiplexer #(.width(16)) multiplexer_2 (
    .in0(lagrangeinterpolationfindvalue_2_out_10), .in1(negator_2_out), .out(y6),
    .sel(lagrangeinterpolationfindvalue_2_out_11));  // open: en

  // Notes on the sheet:
  //   Encryptor and Parity Generator
  //   The user can provide a suitable public key for the decryption.
  //   Working :
  //   This subcircuit works as an encryptor to the inputs that are given, based on the Vignere Cipher.
  //   It also works as a parity generator in the 2nd half, where it generated the parity values, so that in future if some data is lost, then with the help of these, we can recover the original values.
endmodule

// Decrypter
module Decryptor (
  input  [15:0] in_1,
  input  [15:0] in_2,
  input  [15:0] in_3,
  input  [15:0] in_4,
  input  [15:0] in_5,
  output [15:0] out_6,
  output [15:0] out_7,
  output [15:0] out_8,
  output [15:0] out_9
);

  wire [15:0] divider_1_rem, divider_2_rem, divider_3_rem, divider_4_rem, multiplexer_1_out,
       multiplexer_2_out, multiplexer_3_out, multiplexer_4_out, negator_1_out, negator_2_out, negator_3_out,
       negator_4_out, subtractor_1_out, subtractor_2_out, subtractor_3_out, subtractor_4_out,
       subtractor_5_out, subtractor_6_out, subtractor_7_out, subtractor_8_out;

  Subtractor #(.width(16)) subtractor_1 (.a(in_1), .b(in_5), .out(subtractor_1_out));  // open: bin, bout
  Subtractor #(.width(16)) subtractor_2 (.a(in_2), .b(in_5), .out(subtractor_2_out));  // open: bin, bout
  Subtractor #(.width(16)) subtractor_3 (.a(in_3), .b(in_5), .out(subtractor_3_out));  // open: bin, bout
  Subtractor #(.width(16)) subtractor_4 (.a(in_4), .b(in_5), .out(subtractor_4_out));  // open: bin, bout
  Negator #(.width(16)) negator_1 (.in(subtractor_1_out), .out(negator_1_out));
  Negator #(.width(16)) negator_2 (.in(subtractor_2_out), .out(negator_2_out));
  Negator #(.width(16)) negator_3 (.in(subtractor_3_out), .out(negator_3_out));
  Negator #(.width(16)) negator_4 (.in(subtractor_4_out), .out(negator_4_out));
  Multiplexer #(.width(16)) multiplexer_1 (
    .in0(subtractor_1_out), .in1(negator_1_out), .out(multiplexer_1_out), .sel(subtractor_1_out[15]));  // open: en
  Multiplexer #(.width(16)) multiplexer_2 (
    .in0(subtractor_2_out), .in1(negator_2_out), .out(multiplexer_2_out), .sel(subtractor_2_out[15]));  // open: en
  Multiplexer #(.width(16)) multiplexer_3 (
    .in0(subtractor_3_out), .in1(negator_3_out), .out(multiplexer_3_out), .sel(subtractor_3_out[15]));  // open: en
  Multiplexer #(.width(16)) multiplexer_4 (
    .in0(subtractor_4_out), .in1(negator_4_out), .out(multiplexer_4_out), .sel(subtractor_4_out[15]));  // open: en
  Subtractor #(.width(16)) subtractor_5 (.a(16'h10), .b(divider_1_rem), .out(subtractor_5_out));  // open: bin, bout
  Divider #(.width(16)) divider_1 (.a(multiplexer_1_out), .b(16'h10), .rem(divider_1_rem));  // open: out, upper
  Divider #(.width(16)) divider_2 (.a(multiplexer_2_out), .b(16'h10), .rem(divider_2_rem));  // open: out, upper
  Divider #(.width(16)) divider_3 (.a(multiplexer_3_out), .b(16'h10), .rem(divider_3_rem));  // open: out, upper
  Divider #(.width(16)) divider_4 (.a(multiplexer_4_out), .b(16'h10), .rem(divider_4_rem));  // open: out, upper
  Multiplexer #(.width(16)) multiplexer_5 (
    .in0(divider_1_rem), .in1(subtractor_5_out), .out(out_6), .sel(subtractor_1_out[15]));  // open: en
  Subtractor #(.width(16)) subtractor_6 (.a(16'h10), .b(divider_2_rem), .out(subtractor_6_out));  // open: bin, bout
  Multiplexer #(.width(16)) multiplexer_6 (
    .in0(divider_2_rem), .in1(subtractor_6_out), .out(out_7), .sel(subtractor_2_out[15]));  // open: en
  Subtractor #(.width(16)) subtractor_7 (.a(16'h10), .b(divider_3_rem), .out(subtractor_7_out));  // open: bin, bout
  Multiplexer #(.width(16)) multiplexer_7 (
    .in0(divider_3_rem), .in1(subtractor_7_out), .out(out_8), .sel(subtractor_3_out[15]));  // open: en
  Subtractor #(.width(16)) subtractor_8 (.a(16'h10), .b(divider_4_rem), .out(subtractor_8_out));  // open: bin, bout
  Multiplexer #(.width(16)) multiplexer_8 (
    .in0(divider_4_rem), .in1(subtractor_8_out), .out(out_9), .sel(subtractor_4_out[15]));  // open: en

  // Notes on the sheet:
  //   Num1
  //   Num2
  //   Num3
  //   Num4
  //   KEY
  //   The user can provide a suitable public key for the decryption.
  //   Decryptor
  //   Working :
  //   This subcircuit works as an encryptor to the inputs that are given, based on the Vignere Cipher.
endmodule
